# Fritzing sketch Otto DIY Breakout Board3 (saved by Fritzing 0.9.3b)
circuit board: 3.22611cm x 4.1292cm
breadboards: 1

parts:
  WeMos_D1_Mini1 = WeMos D1 Mini
  M1 = Dagu DGServo 9g (Top view) [part_number=RS001B]
  M2 = Dagu DGServo 9g (Top view) [part_number=RS001B]
  M3 = Dagu DGServo 9g (Top view) [part_number=RS001B]
  M4 = Dagu DGServo 9g (Top view) [part_number=RS001B]
  S1 = Toggle Switch [package=THT]
  BATT1 = 4xAA Switchable Battery Pack w/Bare Wire
  hc-sr1 = hc-sr04
  S3 = Toggle Switch [package=THT]  # not connected
  J2 = female pin header, 1 pin [form="♀ (female)"]
  J3 = female pin header, 1 pin [form="♀ (female)"]

nets:
  VCC: WeMos_D1_Mini1.5V, M1.vcc, M2.vcc, M3.vcc, M4.vcc, S1.L2, hc-sr1.VCC
  N1: WeMos_D1_Mini1.D0, M2.pulse
  N2: WeMos_D1_Mini1.D3, hc-sr1.Echo
  N3: WeMos_D1_Mini1.D4, hc-sr1.Trig
  N4: WeMos_D1_Mini1.D5, M4.pulse
  N5: WeMos_D1_Mini1.D6, M1.pulse
  N6: WeMos_D1_Mini1.D7, M3.pulse
  N7: WeMos_D1_Mini1.D8, J2.pin1
  GND: WeMos_D1_Mini1.G, M1.gnd, M2.gnd, M3.gnd, M4.gnd, BATT1.NEG, hc-sr1.GND, J3.pin1
  N8: S1.COM, BATT1.POS

custom parts:
  4xAA Switchable Battery Pack w/Bare Wire: 4xAA Switchable Battery Pack with Bare Wire connection
